// Logisim project FLIP FLOP JK.circ as structural Verilog: 1 circuit, main circuit main
module main (
  input  K,
  input  J,
  output Q,
  output Q1
);

  wire and_1_out, and_2_out, clock_1_out;

  Clock clock_1 (.out(clock_1_out));
  and and_1 (and_1_out, Q, K, clock_1_out);
  and and_2 (and_2_out, clock_1_out, J, Q1);
  nor nor_1 (Q, and_1_out, Q1);
  nor nor_2 (Q1, Q, and_2_out);
endmodule
